// Logisim project Practica4.circ as structural Verilog
module XOR (
  input  P,
  input  Q,
  output P_XOR_Q
);

  wire and_1_out, and_2_out, not_1_out, not_2_out;

  not not_1 (not_1_out, P);
  not not_2 (not_2_out, Q);
  and and_1 (and_1_out, not_1_out, Q);
  and and_2 (and_2_out, P, not_2_out);
  or or_1 (P_XOR_Q, and_1_out, and_2_out);

  // Notes on the sheet:
  //   Compuerta XOR
endmodule

// ALU
module ALU_1_bit_suma (
  input  Ci,
  input  [1:0] Op,
  input  A,
  input  B,
  output S,
  output Ci_1
);

  wire and_1_out, and_2_out, and_3_out, or_1_out, xor_1_p_xor_q, xor_2_p_xor_q;

  and and_1 (and_1_out, B, A);
  and and_2 (and_2_out, A, B);
  or or_1 (or_1_out, A, B);
  XOR xor_1 (.P(A), .Q(B), .P_XOR_Q(xor_1_p_xor_q));
  and and_3 (and_3_out, Ci, xor_1_p_xor_q);
  or or_2 (Ci_1, and_1_out, and_3_out);
  XOR xor_2 (.P(Ci), .Q(xor_1_p_xor_q), .P_XOR_Q(xor_2_p_xor_q));
  Multiplexer #(.select(2)) multiplexer_1 (
    .in0(and_2_out), .in1(or_1_out), .in2(xor_2_p_xor_q), .out(S), .sel(Op));  // open: in3, en

  // Notes on the sheet:
  //   ALU de 1 bit
endmodule

module ALU_8_bits_suma (
  input  C0,
  input  [1:0] Op,
  input  [7:0] A,
  input  [7:0] B,
  output [7:0] A_op_B,
  output Desbordamiento
);

  wire alu_1_bit_suma_1_ci_1, alu_1_bit_suma_2_ci_1, alu_1_bit_suma_3_ci_1, alu_1_bit_suma_4_ci_1,
       alu_1_bit_suma_5_ci_1, alu_1_bit_suma_6_ci_1, alu_1_bit_suma_7_ci_1;

  ALU_1_bit_suma alu_1_bit_suma_1 (.A(A[0]), .B(B[0]), .S(A_op_B[0]), .Ci(C0), .Op(Op), .Ci_1(alu_1_bit_suma_1_ci_1));
  ALU_1_bit_suma alu_1_bit_suma_2 (
    .A(A[1]), .B(B[1]), .S(A_op_B[1]), .Ci(alu_1_bit_suma_1_ci_1), .Op(Op), .Ci_1(alu_1_bit_suma_2_ci_1));
  ALU_1_bit_suma alu_1_bit_suma_3 (
    .A(A[2]), .B(B[2]), .S(A_op_B[2]), .Ci(alu_1_bit_suma_2_ci_1), .Op(Op), .Ci_1(alu_1_bit_suma_3_ci_1));
  ALU_1_bit_suma alu_1_bit_suma_4 (
    .A(A[3]), .B(B[3]), .S(A_op_B[3]), .Ci(alu_1_bit_suma_3_ci_1), .Op(Op), .Ci_1(alu_1_bit_suma_4_ci_1));
  ALU_1_bit_suma alu_1_bit_suma_5 (
    .A(A[4]), .B(B[4]), .S(A_op_B[4]), .Ci(alu_1_bit_suma_4_ci_1), .Op(Op), .Ci_1(alu_1_bit_suma_5_ci_1));
  ALU_1_bit_suma alu_1_bit_suma_6 (
    .A(A[5]), .B(B[5]), .S(A_op_B[5]), .Ci(alu_1_bit_suma_5_ci_1), .Op(Op), .Ci_1(alu_1_bit_suma_6_ci_1));
  ALU_1_bit_suma alu_1_bit_suma_7 (
    .A(A[6]), .B(B[6]), .S(A_op_B[6]), .Ci(alu_1_bit_suma_6_ci_1), .Op(Op), .Ci_1(alu_1_bit_suma_7_ci_1));
  ALU_1_bit_suma alu_1_bit_suma_8 (
    .A(A[7]), .B(B[7]), .S(A_op_B[7]), .Ci(alu_1_bit_suma_7_ci_1), .Op(Op), .Ci_1(Desbordamiento));

  // Notes on the sheet:
  //   ALU de 8 bits
endmodule

module ALU_1_bit_resta (
  input  Ci,
  input  [1:0] Op,
  input  A,
  input  B,
  output S,
  output Ci_1
);

  wire and_1_out, and_2_out, and_3_out, not_1_out, or_2_out, xor_1_p_xor_q, xor_2_p_xor_q, xor_3_p_xor_q,
       xor_4_p_xor_q;

  not not_1 (not_1_out, B);
  XOR xor_1 (.P(A), .Q(B), .P_XOR_Q(xor_1_p_xor_q));
  and and_1 (and_1_out, B, A);
  or or_1 (Ci_1, and_1_out, and_3_out);
  and and_2 (and_2_out, A, B);
  or or_2 (or_2_out, A, B);
  XOR xor_2 (.P(Ci), .Q(xor_1_p_xor_q), .P_XOR_Q(xor_2_p_xor_q));
  and and_3 (and_3_out, Ci, xor_1_p_xor_q);
  Multiplexer #(.select(2)) multiplexer_1 (
    .in0(and_2_out), .in1(or_2_out), .in2(xor_2_p_xor_q), .in3(xor_3_p_xor_q), .out(S), .sel(Op));  // open: en
  XOR xor_3 (.P(xor_4_p_xor_q), .Q(1'b0), .P_XOR_Q(xor_3_p_xor_q));
  XOR xor_4 (.P(1'b1), .Q(not_1_out), .P_XOR_Q(xor_4_p_xor_q));

  // Notes on the sheet:
  //   ALU de 1 bit
endmodule

module ALU (
  input  [7:0] in_1,
  input  [7:0] in_2,
  output [7:0] out_3,
  output [7:0] out_4,
  output [7:0] out_5,
  output [7:0] out_6,
  output [7:0] out_7,
  output [7:0] out_8,
  output [7:0] out_9
);

  wire [7:0] alu_8_bits_suma_3_a_op_b, inv_1_out_2;

  inv inv_1 (.in_1(in_2), .out_2(inv_1_out_2));
  ALU_8_bits_suma alu_8_bits_suma_1 (
    .A(in_1), .B(in_2), .C0(1'b0), .Op(2'b00), .A_op_B(out_3));  // open: Desbordamiento
  ALU_8_bits_suma alu_8_bits_suma_2 (
    .A(in_1), .B(in_2), .C0(1'b0), .Op(2'b01), .A_op_B(out_4));  // open: Desbordamiento
  ALU_8_bits_suma alu_8_bits_suma_3 (
    .A(in_1), .B(in_2), .C0(1'b0), .Op(2'b00), .A_op_B(alu_8_bits_suma_3_a_op_b));  // open: Desbordamiento
  ALU_8_bits_suma alu_8_bits_suma_4 (.C0(1'b0), .Op(2'b00), .A_op_B(out_7));  // open: A, B, Desbordamiento
  ALU_8_bits_suma alu_8_bits_suma_5 (
    .A(in_1), .B(in_2), .C0(1'b0), .Op(2'b10), .A_op_B(out_8));  // open: Desbordamiento
  ALU_8_bits_suma alu_8_bits_suma_6 (
    .A(in_1), .B(inv_1_out_2), .C0(1'b0), .Op(2'b10), .A_op_B(out_9));  // open: Desbordamiento
  assign out_5 = ~alu_8_bits_suma_3_a_op_b;  // NOT_Gate not_1, 8 bits wide
  Multiplexer #(.select(3), .width(8)) multiplexer_1 (
    .out(out_6), .en(1'b1));  // open: in0, in1, in2, in3, in4, in5, in6, in7, sel
endmodule

module inv (
  input  [7:0] in_1,
  output [7:0] out_2
);

  wire [7:0] not_1_out;

  ALU_8_bits_suma alu_8_bits_suma_1 (
    .A(not_1_out), .B(8'h1), .C0(1'b0), .Op(2'b10), .A_op_B(out_2));  // open: Desbordamiento
  assign not_1_out = ~in_1;  // NOT_Gate not_1, 8 bits wide
endmodule
